# Fritzing sketch obniz-handson-circuit-diagram (saved by Fritzing 1.0.5)
breadboards: 1

parts:
  LED1 = LED - 5mm [color="Red (633nm)" current=0.030A package="5 mm [THT]"]
  R1 = Resistor [tolerance=±5% power=0.25W resistance=680 package=THT]
  LED2 = LED - 5mm [color="Green (555nm)" current=0.030A package="5 mm [THT]"]
  R2 = Resistor [tolerance=±5% power=0.25W resistance=470 package=THT]
  LED3 = LED - 5mm [color="Blue (525nm)" current=0.030A package="5 mm [THT]"]
  R3 = Resistor [tolerance=±5% power=0.25W resistance=330 package=THT]
  LED4 = LED - 5mm [color="Orange (620nm)" current=0.030A package="5 mm [THT]"]
  R4 = Resistor [tolerance=±5% power=0.25W resistance=680 package=THT]
  R_CdS = 12mm Trimmer Potentiometer (Large) [maximum_resistance=10kΩ knob_status=50% power=0.5W package=THT]
  CdS_Cell = Photocell (LDR) [power=0.25W dark_resistance_@0.01lx=300kΩ light_resistance_@100lx=400Ω luminance=10lx package=THT]

nets:
  N1: LED1.cathode, R1.Pin_0
  io1: LED1.anode
  GND: R1.Pin_1, R2.Pin_1, R3.Pin_1, R4.Pin_1, R_CdS.wiper
  N2: LED2.cathode, R2.Pin_0
  io2: LED2.anode
  N3: LED3.cathode, R3.Pin_0
  io3: LED3.anode
  N4: LED4.cathode, R4.Pin_0
  io4: LED4.anode
  ad0: R_CdS.leg2, CdS_Cell.pin_1
  5V: CdS_Cell.pin_0
